# Fritzing sketch TrainMicro (saved by Fritzing 0.8.7b)
circuit board: 8.46667cm x 5.64444cm

parts:
  Part1 = Arduino Mega 2560 (Rev3)
  IC1 = ULN2003A [package="SO16 [SMD]"]
  IC2 = ULN2003A [package="SO16 [SMD]"]
  U1 = Optocoupler [package=THT]
  U2 = Optocoupler [package=THT]
  U3 = Optocoupler [package=THT]
  R1 = Resistor [tolerance=±5% resistance=1k package=THT]
  R2 = Resistor [tolerance=±5% resistance=1k package=THT]
  JP1 = Header 8 [package=1x08_smd]
  JP2 = Header 8 [package=1x08_smd]
  U4 = Optocoupler [package=THT]
  R3 = Resistor [tolerance=±5% resistance=1k package=THT]
  R4 = Resistor [tolerance=±5% resistance=1k package=THT]
  U5 = Optocoupler [package=THT]
  U6 = Optocoupler [package=THT]
  R5 = Resistor [tolerance=±5% resistance=1k package=THT]
  R6 = Resistor [tolerance=±5% resistance=1k package=THT]
  JP3 = Header 8 [package=1x08_smd]
  U7 = Optocoupler [package=THT]
  U8 = Optocoupler [package=THT]
  R9 = Resistor [tolerance=±5% resistance=1k package=THT]
  R10 = Resistor [tolerance=±5% resistance=1k package=THT]
  JP6 = Header 4 [package=1x04-smd]
  JP7 = Header 8 [package=1x08_smd]
  U9 = MAX485 [package=dil08]
  U10 = MAX485 [package=dil08]
  JP8 = Header 5 [package=1x05-1mm-ra]
  JP9 = Header 3 [package=1x03-1mm-ra]
  IC3 = Dual Op-Amp [package=dip08]
  R11 = Resistor [tolerance=±5% resistance=470k package=THT]
  R12 = Resistor [tolerance=±5% resistance=10k package=THT]
  R13 = Resistor [tolerance=±5% resistance=10k package=THT]
  JP10 = Header 10 [package=1x10-2mm-smd]
  R14 = Resistor [tolerance=±5% resistance=100k package=THT]
  R15 = Resistor [tolerance=±5% resistance=1k package=THT]
  R16 = Resistor [tolerance=±5% resistance=100k package=THT]
  R17 = Resistor [tolerance=±5% resistance=470k package=THT]
  IC4 = Dual Op-Amp [package=dip08]
  R18 = Resistor [tolerance=±5% resistance=470k package=THT]
  R19 = Resistor [tolerance=±5% resistance=470k package=THT]
  R20 = Resistor [tolerance=±5% resistance=10k package=THT]
  R21 = Resistor [tolerance=±5% resistance=10k package=THT]
  R22 = Resistor [tolerance=±5% resistance=100k package=THT]
  R23 = Resistor [tolerance=±5% resistance=1k package=THT]
  R24 = Resistor [tolerance=±5% resistance=100k package=THT]
  R25 = Resistor [tolerance=±5% resistance=1k package=THT]
  R26 = Resistor [tolerance=±5% resistance=220 package=THT]
  R27 = Resistor [tolerance=±5% resistance=220 package=THT]
  R28 = Resistor [tolerance=±5% resistance=220 package=THT]
  R29 = Resistor [tolerance=±5% resistance=220 package=THT]
  R30 = Resistor [tolerance=±5% resistance=220 package=THT]
  R31 = Resistor [tolerance=±5% resistance=220 package=THT]
  R32 = Resistor [tolerance=±5% resistance=220 package=THT]
  R33 = Resistor [tolerance=±5% resistance=220 package=THT]
  R34 = Resistor [tolerance=±5% resistance=220 package=THT]
  R35 = Resistor [tolerance=±5% resistance=220 package=THT]
  R36 = Resistor [tolerance=±5% resistance=220 package=THT]
  R37 = Resistor [tolerance=±5% resistance=220 package=THT]
  R38 = Resistor [tolerance=±5% resistance=220 package=THT]
  C1 = Electrolytic Capacitor [capacitance=100µF package="200 mil [THT, electrolytic]"]
  C2 = Capacitor [package=cap-pth-small2]
  U11 = DIODE-ZENER [package=diode-zener]
  U12 = Optocoupler [package=THT]
  R39 = Resistor [tolerance=±5% resistance=1k package=THT]
  R40 = Resistor [tolerance=±5% resistance=1k package=THT]
  R41 = Resistor [tolerance=±5% resistance=1k package=THT]

nets (from the schematic view):
  N1: Part1.A0, IC3.B_OUT, R17.Pin_1
  N2: Part1.A1, IC4.B_OUT, R19.Pin_1
  N3: Part1.D19/RX1, U10.RO
  N4: Part1.D18/TX1, U9.DI
  N5: Part1.SCL, R41.Pin_0
  N6: Part1.SDA, R40.Pin_0
  GND: Part1.GND, IC1.0V, IC2.0V, U1.Pin_2, U2.Pin_2, U3.Pin_2, JP1.8, JP2.8, U4.Pin_2, U5.Pin_2, U6.Pin_2, U7.Pin_2, U8.Pin_2, JP6.2, JP6.4, JP7.1, U9.GND, U10.RE, U10.DE, U10.GND, JP8.5, JP9.3, IC3.A_V-, R11.Pin_0, R13.Pin_0, JP10.1, JP10.3, JP10.7, IC4.A_V-, R18.Pin_0, R21.Pin_0, C1.-, C2.2, U11.A, U12.Pin_2, U12.Pin_4
  5V: Part1.VIN, U9.RE, U9.DE, JP9.1, IC3.A_V+, R12.Pin_1, R15.Pin_1, IC4.A_V+, R20.Pin_1, R23.Pin_1, C1.+, C2.1, U11.C
  N7: Part1.D22, R36.Pin_0
  N8: Part1.D23, R34.Pin_0
  N9: Part1.D24, R37.Pin_0
  N10: Part1.D25, R35.Pin_0
  N11: Part1.D26, R38.Pin_0
  N12: Part1.D27, R33.Pin_0
  N13: Part1.D28, R32.Pin_0
  N14: Part1.D29, R31.Pin_0
  N15: Part1.D30, R30.Pin_0
  N16: Part1.D31, R29.Pin_0
  N17: Part1.D32, R28.Pin_0
  N18: Part1.D33, R27.Pin_0
  N19: Part1.D34, R26.Pin_0
  N20: Part1.D35, R25.Pin_0
  N21: Part1.D36, R2.Pin_0
  N22: Part1.D37, R1.Pin_0
  N23: Part1.D38, R3.Pin_0
  N24: Part1.D39, R4.Pin_0
  N25: Part1.D40, R5.Pin_0
  N26: Part1.D41, R6.Pin_0
  N27: Part1.D42, R10.Pin_1
  N28: Part1.D43, R9.Pin_1
  N29: Part1.D45, R39.Pin_0
  N30: Part1.D47, JP7.8
  N31: Part1.D48, JP7.7
  N32: Part1.D49, JP7.6
  N33: Part1.D50, JP7.5
  N34: Part1.D51, JP7.4
  N35: Part1.D52, JP7.3
  N36: Part1.D53, JP7.2
  N37: IC1.In_1, R36.Pin_1
  N38: IC1.In_2, R34.Pin_1
  N39: IC1.In_3, R37.Pin_1
  N40: IC1.In_4, R35.Pin_1
  N41: IC1.In_5, R38.Pin_1
  N42: IC1.In_6, R33.Pin_1
  N43: IC1.In_7, R32.Pin_1
  24V: IC1.COM_-_Common, IC2.COM_-_Common, U1.Pin_5, U2.Pin_5, U4.Pin_5, U5.Pin_5, U6.Pin_5, JP3.2, U7.Pin_5, U8.Pin_5
  N44: IC1.Out_7, JP1.7
  N45: IC1.Out_6, JP1.6
  N46: IC1.Out_5, JP1.5
  N47: IC1.Out_4, JP1.4
  N48: IC1.Out_3, JP1.3
  N49: IC1.Out_2, JP1.2
  N50: IC1.Out_1, JP1.1
  N51: IC2.In_1, R31.Pin_1
  N52: IC2.In_2, R30.Pin_1
  N53: IC2.In_3, R29.Pin_1
  N54: IC2.In_4, R28.Pin_1
  N55: IC2.In_5, R27.Pin_1
  N56: IC2.In_6, R26.Pin_1
  N57: IC2.In_7, R25.Pin_1
  N58: IC2.Out_7, JP2.7
  N59: IC2.Out_6, JP2.6
  N60: IC2.Out_5, JP2.5
  N61: IC2.Out_4, JP2.4
  N62: IC2.Out_3, JP2.3
  N63: IC2.Out_2, JP2.2
  N64: IC2.Out_1, JP2.1
  N65: U1.Pin_1, R1.Pin_1
  N66: U1.Pin_4, JP3.7
  N67: U2.Pin_1, R3.Pin_1
  N68: U2.Pin_4, JP3.3
  N69: U3.Pin_1, R2.Pin_1
  N70: U3.Pin_4, JP3.8
  N71: U4.Pin_1, R4.Pin_1
  N72: U4.Pin_4, JP3.4
  N73: U5.Pin_1, R5.Pin_1
  N74: U5.Pin_4, JP3.5
  N75: U6.Pin_1, R6.Pin_1
  N76: U6.Pin_4, JP3.6
  N77: U7.Pin_1, R9.Pin_0
  N78: U7.Pin_4, JP6.1
  N79: U8.Pin_1, R10.Pin_0
  N80: U8.Pin_4, JP6.3
  N81: U9.A, JP8.1
  N82: U9.B, JP8.2
  VCC: U9.VCC, U10.VCC
  N83: U10.A, JP8.3
  N84: U10.B, JP8.4
  N85: IC3.A_OUT, R14.Pin_0, R16.Pin_1
  N86: IC3.A_-IN, R11.Pin_1, R16.Pin_0
  N87: IC3.A_+IN, R12.Pin_0
  N88: IC3.B_+IN, JP10.2, R15.Pin_0
  N89: IC3.B_-IN, R14.Pin_1, R17.Pin_0
  N90: JP10.4, IC4.B_+IN, R23.Pin_0
  N91: JP10.6, U12.Pin_5
  N92: JP10.9, R40.Pin_1
  N93: JP10.10, R41.Pin_1
  N94: IC4.A_OUT, R22.Pin_0, R24.Pin_1
  N95: IC4.A_-IN, R18.Pin_1, R24.Pin_0
  N96: IC4.A_+IN, R20.Pin_0
  N97: IC4.B_-IN, R19.Pin_0, R22.Pin_1
  N98: U12.Pin_1, R39.Pin_1

notes:
  LED Out
  Relay Control 1
  Relay Control 2
  Traction Control
  Relay Input
  RS422 Coms
  5V Power
